# Fritzing sketch interfon (saved by Fritzing 0.9.4)
breadboards: 1

parts:
  J1 = Screw terminal - 2 pins [package=THT]
  J2 = Screw terminal - 2 pins [package=THT]
  V1 = DC Power [voltage=24]
  R1 = Resistor [tolerance=±5% resistance=1k package="2010 [SMD]"]
  C1 = Ceramic Capacitor [capacitance="100 nF" package="0805 [SMD, multilayer]"]
  C2 = Ceramic Capacitor [capacitance="100 nF" package="0805 [SMD, multilayer]"]
  SP1 = SPEAKER [package=pcb_mount_speaker]
  D1 = Zener Diode [part_number=1N4732A breakdown_voltage=12.1V package="300 mil [THT]"]
  C3 = Ceramic Capacitor [capacitance="100 nF" package="0805 [SMD, multilayer]"]
  SP2 = SPEAKER [package=pcb_mount_speaker]
  D2 = Zener Diode [part_number=1N4732A breakdown_voltage=12.1V package="300 mil [THT]"]

nets:
  N1: J1.pin1, R1.Pin_1, C1.0, C2.0, SP1.-
  N2: J1.pin2, J2.pin1, D1.cathode, D2.anode
  N3: J2.pin2, V1.V-, C1.1, C3.1, SP2.+
  N4: V1.V+, R1.Pin_0
  N5: C2.1, SP1.+, D1.anode
  N6: C3.0, SP2.-, D2.cathode
